// Logisim project Cosmic1.circ as structural Verilog: 3 circuits, main circuit main
module main (
  input  Reset,
  input  CLK_En,
  output [15:0] Instruction
);

  wire and_1_out, CLK_out, nand_1_out, nand_2_out, nand_3_out, nand_4_out, nand_5_out, nand_6_out,
       nand_7_out, nand_8_out, nand_9_out, nand_10_out, nand_11_out, nand_12_out, nand_13_out, nand_14_out,
       nand_15_out, nand_16_out, nand_17_out, nand_18_out, nand_19_out, nand_20_out, nand_21_out,
       nand_22_out, nand_23_out, nand_24_out, nand_25_out, nand_26_out, nand_27_out, nand_28_out,
       nand_29_out, nand_30_out, nand_31_out, nand_32_out, nand_33_out, nand_34_out, nand_35_out,
       nand_36_out, nand_37_out, nand_38_out, nand_39_out, nand_40_out, nand_41_out, nand_42_out,
       nand_43_out, nand_44_out, nand_45_out, nand_46_out, nand_47_out, nand_48_out, nand_49_out,
       nand_50_out, nand_51_out, nand_52_out, nand_53_out, nand_54_out, nand_55_out, nand_56_out,
       nand_57_out, nand_58_out, nand_59_out, nand_60_out, nand_62_out, nand_64_out, nand_66_out,
       nand_68_out, nand_70_out, nand_72_out, nand_74_out, nand_76_out, nand_78_out, nand_80_out, not_1_out,
       or_1_out, or_2_out, or_3_out, or_4_out, or_5_out, or_6_out, or_7_out, or_8_out, or_9_out, or_10_out,
       or_11_out, or_12_out, or_13_out, or_14_out;
  wire [9:0] nand_61_out;
  wire [15:0] and_2_out;

  Clock #(.highDuration(2), .lowDuration(2)) CLK (.out(CLK_out));
  not not_1 (not_1_out, and_2_out[1]);
  and and_1 (and_1_out, CLK_out, or_1_out);
  or or_1 (or_1_out, CLK_En, not_1_out);
  nand nand_1 (nand_1_out, nand_62_out, and_1_out);
  or or_2 (or_2_out, nand_22_out, Reset);
  nand nand_2 (nand_2_out, and_1_out, nand_61_out[0]);
  nand nand_3 (nand_3_out, nand_64_out, nand_61_out[0]);
  or or_3 (or_3_out, nand_24_out, Reset);
  nand nand_4 (nand_4_out, nand_61_out[0], nand_61_out[1]);
  nand nand_5 (nand_5_out, nand_66_out, nand_61_out[1]);
  or or_4 (or_4_out, nand_26_out, Reset);
  nand nand_6 (nand_6_out, nand_61_out[1], nand_61_out[2]);
  nand nand_7 (nand_7_out, nand_68_out, nand_61_out[2]);
  or or_5 (or_5_out, nand_28_out, Reset);
  nand nand_8 (nand_8_out, nand_61_out[2], nand_61_out[3]);
  nand nand_9 (nand_9_out, nand_70_out, nand_61_out[3]);
  or or_6 (or_6_out, nand_30_out, Reset);
  nand nand_10 (nand_10_out, nand_61_out[3], nand_61_out[4]);
  nand nand_11 (nand_11_out, nand_72_out, nand_61_out[4]);
  or or_7 (or_7_out, nand_32_out, Reset);
  nand nand_12 (nand_12_out, nand_61_out[4], nand_61_out[5]);
  nand nand_13 (nand_13_out, nand_74_out, nand_61_out[5]);
  or or_8 (or_8_out, nand_34_out, Reset);
  nand nand_14 (nand_14_out, nand_61_out[5], nand_61_out[6]);
  nand nand_15 (nand_15_out, nand_76_out, nand_61_out[6]);
  or or_9 (or_9_out, nand_36_out, Reset);
  nand nand_16 (nand_16_out, nand_61_out[6], nand_61_out[7]);
  nand nand_17 (nand_17_out, nand_78_out, nand_61_out[7]);
  or or_10 (or_10_out, nand_38_out, Reset);
  nand nand_18 (nand_18_out, nand_61_out[7], nand_61_out[8]);
  nand nand_19 (nand_19_out, nand_80_out, nand_61_out[8]);
  or or_11 (or_11_out, nand_40_out, Reset);
  nand nand_20 (nand_20_out, nand_61_out[8], nand_61_out[9]);
  nand nand_21 (nand_21_out, nand_1_out, or_2_out);
  nand nand_22 (nand_22_out, nand_21_out, nand_2_out);
  nand nand_23 (nand_23_out, nand_3_out, or_3_out);
  nand nand_24 (nand_24_out, nand_23_out, nand_4_out);
  nand nand_25 (nand_25_out, nand_5_out, or_4_out);
  nand nand_26 (nand_26_out, nand_25_out, nand_6_out);
  nand nand_27 (nand_27_out, nand_7_out, or_5_out);
  nand nand_28 (nand_28_out, nand_27_out, nand_8_out);
  nand nand_29 (nand_29_out, nand_9_out, or_6_out);
  nand nand_30 (nand_30_out, nand_29_out, nand_10_out);
  nand nand_31 (nand_31_out, nand_11_out, or_7_out);
  nand nand_32 (nand_32_out, nand_31_out, nand_12_out);
  nand nand_33 (nand_33_out, nand_13_out, or_8_out);
  nand nand_34 (nand_34_out, nand_33_out, nand_14_out);
  nand nand_35 (nand_35_out, nand_15_out, or_9_out);
  nand nand_36 (nand_36_out, nand_35_out, nand_16_out);
  nand nand_37 (nand_37_out, nand_17_out, or_10_out);
  nand nand_38 (nand_38_out, nand_37_out, nand_18_out);
  nand nand_39 (nand_39_out, nand_19_out, or_11_out);
  nand nand_40 (nand_40_out, nand_39_out, nand_20_out);
  nand nand_41 (nand_41_out, nand_21_out, ~and_1_out);  // NAND_Gate
  nand nand_42 (nand_42_out, ~and_1_out, nand_22_out);  // NAND_Gate
  nand nand_43 (nand_43_out, nand_23_out, ~nand_61_out[0]);  // NAND_Gate
  nand nand_44 (nand_44_out, ~nand_61_out[0], nand_24_out);  // NAND_Gate
  nand nand_45 (nand_45_out, nand_25_out, ~nand_61_out[1]);  // NAND_Gate
  nand nand_46 (nand_46_out, ~nand_61_out[1], nand_26_out);  // NAND_Gate
  nand nand_47 (nand_47_out, nand_27_out, ~nand_61_out[2]);  // NAND_Gate
  nand nand_48 (nand_48_out, ~nand_61_out[2], nand_28_out);  // NAND_Gate
  nand nand_49 (nand_49_out, nand_29_out, ~nand_61_out[3]);  // NAND_Gate
  nand nand_50 (nand_50_out, ~nand_61_out[3], nand_30_out);  // NAND_Gate
  nand nand_51 (nand_51_out, nand_31_out, ~nand_61_out[4]);  // NAND_Gate
  nand nand_52 (nand_52_out, ~nand_61_out[4], nand_32_out);  // NAND_Gate
  nand nand_53 (nand_53_out, nand_33_out, ~nand_61_out[5]);  // NAND_Gate
  nand nand_54 (nand_54_out, ~nand_61_out[5], nand_34_out);  // NAND_Gate
  nand nand_55 (nand_55_out, nand_35_out, ~nand_61_out[6]);  // NAND_Gate
  nand nand_56 (nand_56_out, ~nand_61_out[6], nand_36_out);  // NAND_Gate
  nand nand_57 (nand_57_out, nand_37_out, ~nand_61_out[7]);  // NAND_Gate
  nand nand_58 (nand_58_out, ~nand_61_out[7], nand_38_out);  // NAND_Gate
  nand nand_59 (nand_59_out, nand_39_out, ~nand_61_out[8]);  // NAND_Gate
  nand nand_60 (nand_60_out, ~nand_61_out[8], nand_40_out);  // NAND_Gate
  nand nand_61 (nand_61_out[0], nand_41_out, nand_62_out);
  nand nand_62 (nand_62_out, nand_61_out[0], nand_42_out);
  nand nand_63 (nand_61_out[1], nand_43_out, nand_64_out);
  nand nand_64 (nand_64_out, nand_61_out[1], nand_44_out);
  nand nand_65 (nand_61_out[2], nand_45_out, nand_66_out);
  nand nand_66 (nand_66_out, nand_61_out[2], nand_46_out);
  nand nand_67 (nand_61_out[3], nand_47_out, nand_68_out);
  nand nand_68 (nand_68_out, nand_61_out[3], nand_48_out);
  nand nand_69 (nand_61_out[4], nand_49_out, nand_70_out);
  nand nand_70 (nand_70_out, nand_61_out[4], nand_50_out);
  nand nand_71 (nand_61_out[5], nand_51_out, nand_72_out);
  nand nand_72 (nand_72_out, nand_61_out[5], nand_52_out);
  nand nand_73 (nand_61_out[6], nand_53_out, nand_74_out);
  nand nand_74 (nand_74_out, nand_61_out[6], nand_54_out);
  nand nand_75 (nand_61_out[7], nand_55_out, nand_76_out);
  nand nand_76 (nand_76_out, nand_61_out[7], nand_56_out);
  nand nand_77 (nand_61_out[8], nand_57_out, nand_78_out);
  nand nand_78 (nand_78_out, nand_61_out[8], nand_58_out);
  nand nand_79 (nand_61_out[9], nand_59_out, nand_80_out);
  nand nand_80 (nand_80_out, nand_61_out[9], nand_60_out);
  ROM #(.addrWidth(10), .dataWidth(16)) rom_1 (.addr(nand_61_out), .data(Instruction));  // open: sel
  and and_2 (and_2_out[0], ~Instruction[12], ~Instruction[13], ~Instruction[14], ~Instruction[15]);  // AND_Gate
  and and_3 (and_2_out[4], ~Instruction[12], ~Instruction[13], Instruction[14], ~Instruction[15]);  // AND_Gate
  and and_4 (and_2_out[8], ~Instruction[12], ~Instruction[13], ~Instruction[14], Instruction[15]);  // AND_Gate
  and and_5 (and_2_out[12], ~Instruction[12], ~Instruction[13], Instruction[14], Instruction[15]);  // AND_Gate
  and and_6 (and_2_out[1], Instruction[12], ~Instruction[13], ~Instruction[14], ~Instruction[15]);  // AND_Gate
  and and_7 (and_2_out[5], Instruction[12], ~Instruction[13], Instruction[14], ~Instruction[15]);  // AND_Gate
  and and_8 (and_2_out[9], Instruction[12], ~Instruction[13], ~Instruction[14], Instruction[15]);  // AND_Gate
  and and_9 (and_2_out[13], Instruction[12], ~Instruction[13], Instruction[14], Instruction[15]);  // AND_Gate
  or or_12 (or_12_out, and_2_out[3], and_2_out[5], and_2_out[6]);
  or or_13 (or_13_out, and_2_out[4], and_2_out[5], and_2_out[6]);
  or or_14 (or_14_out, and_2_out[4], and_2_out[5]);
  and and_10 (and_2_out[2], ~Instruction[12], Instruction[13], ~Instruction[14], ~Instruction[15]);  // AND_Gate
  and and_11 (and_2_out[6], ~Instruction[12], Instruction[13], Instruction[14], ~Instruction[15]);  // AND_Gate
  and and_12 (and_2_out[10], ~Instruction[12], Instruction[13], ~Instruction[14], Instruction[15]);  // AND_Gate
  and and_13 (and_2_out[14], ~Instruction[12], Instruction[13], Instruction[14], Instruction[15]);  // AND_Gate
  and and_14 (and_2_out[3], Instruction[12], Instruction[13], ~Instruction[14], ~Instruction[15]);  // AND_Gate
  and and_15 (and_2_out[7], Instruction[12], Instruction[13], Instruction[14], ~Instruction[15]);  // AND_Gate
  and and_16 (and_2_out[11], Instruction[12], Instruction[13], ~Instruction[14], Instruction[15]);  // AND_Gate
  and and_17 (and_2_out[15], Instruction[12], Instruction[13], Instruction[14], Instruction[15]);
  ALU alu_1 (
    .RSH(and_2_out[7]), .OR(or_14_out), .FC(or_13_out), .CIn(and_2_out[3]), .nA(and_2_out[5]), .nB(or_12_out));  // open: Reg_A, Reg_B, Reg_C

  // Notes on the sheet:
  //   contents of rom_1 (hex, n*v repeats v):
  //   812a 8209 8303 8402 7105 2525 3535 c00a 3f15 1000 354e bc0e 9f01 a00a d000
  //   PAS
  //   NOR
  //   LDI
  //   CAL
  //   HAL
  //   AND
  //   ADI
  //   RET
  //   ADD
  //   XOR
  //   JMP
  //   SUB
  //   RSH
  //   BRH
endmodule

module _16_Byte_Mem (
  input  Reset,
  input  Set,
  input  [7:0] Data_In,
  input  [3:0] Address,
  input  Read,
  output [7:0] Data_Out
);

  wire and_17_out, and_18_out, and_20_out, and_21_out, and_23_out, and_24_out, and_26_out, and_27_out,
       and_29_out, and_30_out, and_33_out, and_34_out, and_37_out, and_38_out, and_41_out, and_42_out,
       and_45_out, and_46_out, and_49_out, and_50_out, and_53_out, and_54_out, and_57_out, and_58_out,
       and_61_out, and_62_out, and_65_out, and_66_out, and_69_out, and_70_out, and_73_out, and_74_out,
       and_77_out, and_79_out, and_81_out, and_83_out, and_85_out, and_86_out, and_87_out, and_88_out,
       and_89_out, and_90_out, and_93_out, and_94_out, and_97_out, and_98_out, and_101_out, and_102_out,
       and_105_out, and_106_out, and_109_out, and_110_out, and_113_out, and_114_out, and_117_out,
       and_118_out, and_121_out, and_122_out, and_125_out, and_126_out, and_129_out, and_130_out,
       and_133_out, and_134_out, and_137_out, and_138_out, and_141_out, and_142_out, and_145_out,
       and_146_out, and_149_out, and_150_out, and_153_out, and_154_out, and_155_out, and_156_out,
       and_157_out, and_158_out, and_161_out, and_162_out, and_165_out, and_166_out, and_169_out,
       and_170_out, and_173_out, and_174_out, and_177_out, and_178_out, and_181_out, and_182_out,
       and_185_out, and_186_out, and_189_out, and_190_out, and_193_out, and_194_out, and_197_out,
       and_198_out, and_201_out, and_202_out, and_205_out, and_206_out, and_209_out, and_210_out,
       and_213_out, and_214_out, and_217_out, and_218_out, and_221_out, and_222_out, and_224_out,
       and_225_out, and_227_out, and_228_out, and_230_out, and_231_out, and_233_out, and_234_out,
       and_237_out, and_238_out, and_241_out, and_242_out, and_245_out, and_246_out, and_249_out,
       and_250_out, and_253_out, and_254_out, and_257_out, and_258_out, and_261_out, and_262_out,
       and_265_out, and_266_out, and_269_out, and_270_out, and_273_out, and_274_out, and_277_out,
       and_278_out, and_281_out, and_283_out, and_285_out, and_287_out, nor_2_out, nor_4_out, nor_6_out,
       nor_8_out, nor_10_out, nor_12_out, nor_14_out, nor_16_out, nor_18_out, nor_20_out, nor_22_out,
       nor_24_out, nor_26_out, nor_28_out, nor_30_out, nor_32_out, nor_34_out, nor_36_out, nor_38_out,
       nor_40_out, nor_42_out, nor_44_out, nor_46_out, nor_48_out, nor_50_out, nor_52_out, nor_54_out,
       nor_56_out, nor_58_out, nor_60_out, nor_62_out, nor_64_out, nor_66_out, nor_68_out, nor_70_out,
       nor_72_out, nor_74_out, nor_76_out, nor_78_out, nor_80_out, nor_82_out, nor_84_out, nor_86_out,
       nor_88_out, nor_90_out, nor_92_out, nor_94_out, nor_96_out, nor_98_out, nor_100_out, nor_102_out,
       nor_104_out, nor_106_out, nor_108_out, nor_110_out, nor_112_out, nor_114_out, nor_116_out,
       nor_118_out, nor_120_out, nor_122_out, nor_124_out, nor_126_out, nor_128_out, nor_130_out,
       nor_132_out, nor_134_out, nor_136_out, nor_138_out, nor_140_out, nor_142_out, nor_144_out,
       nor_146_out, nor_148_out, nor_150_out, nor_152_out, nor_154_out, nor_156_out, nor_158_out,
       nor_160_out, nor_162_out, nor_164_out, nor_166_out, nor_168_out, nor_170_out, nor_172_out,
       nor_174_out, nor_176_out, nor_178_out, nor_180_out, nor_182_out, nor_184_out, nor_186_out,
       nor_188_out, nor_190_out, nor_192_out, nor_194_out, nor_196_out, nor_198_out, nor_200_out,
       nor_202_out, nor_204_out, nor_206_out, nor_208_out, nor_210_out, nor_212_out, nor_214_out,
       nor_216_out, nor_218_out, nor_220_out, nor_222_out, nor_224_out, nor_226_out, nor_228_out,
       nor_230_out, nor_232_out, nor_234_out, nor_236_out, nor_238_out, nor_240_out, nor_242_out,
       nor_244_out, nor_246_out, nor_248_out, nor_250_out, nor_252_out, nor_254_out, nor_256_out;
  wire [7:0] _0, _1, _2, _3, _4, _5, _6, _7, _8, _9, _10, _11, _12, _13, _14, _15, nor_1_out, nor_9_out,
       nor_17_out, nor_25_out, nor_65_out, nor_73_out, nor_81_out, nor_89_out, nor_129_out, nor_137_out,
       nor_145_out, nor_153_out, nor_193_out, nor_201_out, nor_209_out, nor_217_out, or_1_out, or_2_out,
       or_3_out, or_4_out;
  wire [15:0] and_1_out;

  and and_1 (and_1_out[0], ~Address[0], ~Address[1], ~Address[2], ~Address[3]);  // AND_Gate
  and and_2 (and_1_out[4], ~Address[0], ~Address[1], Address[2], ~Address[3]);  // AND_Gate
  and and_3 (and_1_out[8], ~Address[0], ~Address[1], ~Address[2], Address[3]);  // AND_Gate
  and and_4 (and_1_out[12], ~Address[0], ~Address[1], Address[2], Address[3]);  // AND_Gate
  and and_5 (and_1_out[1], Address[0], ~Address[1], ~Address[2], ~Address[3]);  // AND_Gate
  and and_6 (and_1_out[5], Address[0], ~Address[1], Address[2], ~Address[3]);  // AND_Gate
  and and_7 (and_1_out[9], Address[0], ~Address[1], ~Address[2], Address[3]);  // AND_Gate
  and and_8 (and_1_out[13], Address[0], ~Address[1], Address[2], Address[3]);  // AND_Gate
  assign or_1_out = _0 | _1 | _2 | _3;  // OR_Gate or_1, 8 bits wide
  assign or_2_out = _4 | _5 | _6 | _7;  // OR_Gate or_2, 8 bits wide
  assign or_3_out = _8 | _9 | _10 | _11;  // OR_Gate or_3, 8 bits wide
  assign or_4_out = _12 | _13 | _14 | _15;  // OR_Gate or_4, 8 bits wide
  and and_9 (and_1_out[2], ~Address[0], Address[1], ~Address[2], ~Address[3]);  // AND_Gate
  and and_10 (and_1_out[6], ~Address[0], Address[1], Address[2], ~Address[3]);  // AND_Gate
  and and_11 (and_1_out[10], ~Address[0], Address[1], ~Address[2], Address[3]);  // AND_Gate
  and and_12 (and_1_out[14], ~Address[0], Address[1], Address[2], Address[3]);  // AND_Gate
  assign Data_Out = or_1_out | or_2_out | or_3_out | or_4_out;  // OR_Gate or_5, 8 bits wide
  and and_13 (and_1_out[3], Address[0], Address[1], ~Address[2], ~Address[3]);  // AND_Gate
  and and_14 (and_1_out[7], Address[0], Address[1], Address[2], ~Address[3]);  // AND_Gate
  and and_15 (and_1_out[11], Address[0], Address[1], ~Address[2], Address[3]);  // AND_Gate
  and and_16 (and_1_out[15], Address[0], Address[1], Address[2], Address[3]);
  and and_17 (and_17_out, and_1_out[0], Data_In[0], Set);
  and and_18 (and_18_out, and_1_out[0], Reset);
  and and_19 (_0[0], and_1_out[0], nor_1_out[0], Read);
  and and_20 (and_20_out, and_1_out[4], Data_In[0], Set);
  and and_21 (and_21_out, and_1_out[4], Reset);
  and and_22 (_4[0], and_1_out[4], nor_9_out[0], Read);
  and and_23 (and_23_out, and_1_out[8], Data_In[0], Set);
  and and_24 (and_24_out, and_1_out[8], Reset);
  and and_25 (_8[0], and_1_out[8], nor_17_out[0], Read);
  and and_26 (and_26_out, and_1_out[12], Data_In[0], Set);
  and and_27 (and_27_out, and_1_out[12], Reset);
  and and_28 (_12[0], and_1_out[12], nor_25_out[0], Read);
  and and_29 (and_29_out, and_1_out[0], Data_In[2], Set);
  and and_30 (and_30_out, and_1_out[0], Data_In[1], Set);
  nor nor_1 (nor_1_out[0], and_18_out, nor_2_out);
  nor nor_2 (nor_2_out, nor_1_out[0], and_17_out);
  nor nor_3 (nor_1_out[1], and_18_out, nor_4_out);
  nor nor_4 (nor_4_out, nor_1_out[1], and_30_out);
  nor nor_5 (nor_1_out[2], and_18_out, nor_6_out);
  nor nor_6 (nor_6_out, nor_1_out[2], and_29_out);
  nor nor_7 (nor_1_out[3], and_18_out, nor_8_out);
  nor nor_8 (nor_8_out, nor_1_out[3], and_46_out);
  and and_31 (_0[2], and_1_out[0], nor_1_out[2], Read);
  and and_32 (_0[1], and_1_out[0], nor_1_out[1], Read);
  and and_33 (and_33_out, and_1_out[4], Data_In[1], Set);
  and and_34 (and_34_out, and_1_out[4], Data_In[2], Set);
  nor nor_9 (nor_9_out[0], and_21_out, nor_10_out);
  nor nor_10 (nor_10_out, nor_9_out[0], and_20_out);
  nor nor_11 (nor_9_out[1], and_21_out, nor_12_out);
  nor nor_12 (nor_12_out, nor_9_out[1], and_33_out);
  nor nor_13 (nor_9_out[2], and_21_out, nor_14_out);
  nor nor_14 (nor_14_out, nor_9_out[2], and_34_out);
  nor nor_15 (nor_9_out[3], and_21_out, nor_16_out);
  nor nor_16 (nor_16_out, nor_9_out[3], and_50_out);
  and and_35 (_4[1], and_1_out[4], nor_9_out[1], Read);
  and and_36 (_4[2], and_1_out[4], nor_9_out[2], Read);
  and and_37 (and_37_out, and_1_out[8], Data_In[1], Set);
  and and_38 (and_38_out, and_1_out[8], Data_In[2], Set);
  nor nor_17 (nor_17_out[0], and_24_out, nor_18_out);
  nor nor_18 (nor_18_out, nor_17_out[0], and_23_out);
  nor nor_19 (nor_17_out[1], and_24_out, nor_20_out);
  nor nor_20 (nor_20_out, nor_17_out[1], and_37_out);
  nor nor_21 (nor_17_out[2], and_24_out, nor_22_out);
  nor nor_22 (nor_22_out, nor_17_out[2], and_38_out);
  nor nor_23 (nor_17_out[3], and_24_out, nor_24_out);
  nor nor_24 (nor_24_out, nor_17_out[3], and_53_out);
  and and_39 (_8[1], and_1_out[8], nor_17_out[1], Read);
  and and_40 (_8[2], and_1_out[8], nor_17_out[2], Read);
  and and_41 (and_41_out, and_1_out[12], Data_In[1], Set);
  and and_42 (and_42_out, and_1_out[12], Data_In[2], Set);
  nor nor_25 (nor_25_out[0], and_27_out, nor_26_out);
  nor nor_26 (nor_26_out, nor_25_out[0], and_26_out);
  nor nor_27 (nor_25_out[1], and_27_out, nor_28_out);
  nor nor_28 (nor_28_out, nor_25_out[1], and_41_out);
  nor nor_29 (nor_25_out[2], and_27_out, nor_30_out);
  nor nor_30 (nor_30_out, nor_25_out[2], and_42_out);
  nor nor_31 (nor_25_out[3], and_27_out, nor_32_out);
  nor nor_32 (nor_32_out, nor_25_out[3], and_57_out);
  and and_43 (_12[1], and_1_out[12], nor_25_out[1], Read);
  and and_44 (_12[2], and_1_out[12], nor_25_out[2], Read);
  and and_45 (and_45_out, and_1_out[0], Data_In[4], Set);
  and and_46 (and_46_out, and_1_out[0], Data_In[3], Set);
  and and_47 (_0[3], and_1_out[0], nor_1_out[3], Read);
  and and_48 (_0[4], and_1_out[0], nor_1_out[4], Read);
  and and_49 (and_49_out, and_1_out[4], Data_In[4], Set);
  and and_50 (and_50_out, and_1_out[4], Data_In[3], Set);
  and and_51 (_4[4], and_1_out[4], nor_9_out[4], Read);
  and and_52 (_4[3], and_1_out[4], nor_9_out[3], Read);
  and and_53 (and_53_out, and_1_out[8], Data_In[3], Set);
  and and_54 (and_54_out, and_1_out[8], Data_In[4], Set);
  and and_55 (_8[3], and_1_out[8], nor_17_out[3], Read);
  and and_56 (_8[4], and_1_out[8], nor_17_out[4], Read);
  and and_57 (and_57_out, and_1_out[12], Data_In[3], Set);
  and and_58 (and_58_out, and_1_out[12], Data_In[4], Set);
  and and_59 (_12[3], and_1_out[12], nor_25_out[3], Read);
  and and_60 (_12[4], and_1_out[12], nor_25_out[4], Read);
  and and_61 (and_61_out, and_1_out[0], Data_In[5], Set);
  and and_62 (and_62_out, and_1_out[0], Data_In[6], Set);
  and and_63 (_0[5], and_1_out[0], nor_1_out[5], Read);
  and and_64 (_0[6], and_1_out[0], nor_1_out[6], Read);
  and and_65 (and_65_out, and_1_out[4], Data_In[5], Set);
  and and_66 (and_66_out, and_1_out[4], Data_In[6], Set);
  and and_67 (_4[5], and_1_out[4], nor_9_out[5], Read);
  and and_68 (_4[6], and_1_out[4], nor_9_out[6], Read);
  and and_69 (and_69_out, and_1_out[8], Data_In[5], Set);
  and and_70 (and_70_out, and_1_out[8], Data_In[6], Set);
  and and_71 (_8[5], and_1_out[8], nor_17_out[5], Read);
  and and_72 (_8[6], and_1_out[8], nor_17_out[6], Read);
  and and_73 (and_73_out, and_1_out[12], Data_In[5], Set);
  and and_74 (and_74_out, and_1_out[12], Data_In[6], Set);
  and and_75 (_12[6], and_1_out[12], nor_25_out[6], Read);
  and and_76 (_12[5], and_1_out[12], nor_25_out[5], Read);
  and and_77 (and_77_out, and_1_out[0], Data_In[7], Set);
  nor nor_33 (nor_1_out[4], and_18_out, nor_34_out);
  nor nor_34 (nor_34_out, nor_1_out[4], and_45_out);
  nor nor_35 (nor_1_out[5], and_18_out, nor_36_out);
  nor nor_36 (nor_36_out, nor_1_out[5], and_61_out);
  nor nor_37 (nor_1_out[6], and_18_out, nor_38_out);
  nor nor_38 (nor_38_out, nor_1_out[6], and_62_out);
  nor nor_39 (nor_1_out[7], and_18_out, nor_40_out);
  nor nor_40 (nor_40_out, nor_1_out[7], and_77_out);
  and and_78 (_0[7], and_1_out[0], nor_1_out[7], Read);
  and and_79 (and_79_out, and_1_out[4], Data_In[7], Set);
  nor nor_41 (nor_9_out[4], and_21_out, nor_42_out);
  nor nor_42 (nor_42_out, nor_9_out[4], and_49_out);
  nor nor_43 (nor_9_out[5], and_21_out, nor_44_out);
  nor nor_44 (nor_44_out, nor_9_out[5], and_65_out);
  nor nor_45 (nor_9_out[6], and_21_out, nor_46_out);
  nor nor_46 (nor_46_out, nor_9_out[6], and_66_out);
  nor nor_47 (nor_9_out[7], and_21_out, nor_48_out);
  nor nor_48 (nor_48_out, nor_9_out[7], and_79_out);
  and and_80 (_4[7], and_1_out[4], nor_9_out[7], Read);
  and and_81 (and_81_out, and_1_out[8], Data_In[7], Set);
  nor nor_49 (nor_17_out[4], and_24_out, nor_50_out);
  nor nor_50 (nor_50_out, nor_17_out[4], and_54_out);
  nor nor_51 (nor_17_out[5], and_24_out, nor_52_out);
  nor nor_52 (nor_52_out, nor_17_out[5], and_69_out);
  nor nor_53 (nor_17_out[6], and_24_out, nor_54_out);
  nor nor_54 (nor_54_out, nor_17_out[6], and_70_out);
  nor nor_55 (nor_17_out[7], and_24_out, nor_56_out);
  nor nor_56 (nor_56_out, nor_17_out[7], and_81_out);
  and and_82 (_8[7], and_1_out[8], nor_17_out[7], Read);
  and and_83 (and_83_out, and_1_out[12], Data_In[7], Set);
  nor nor_57 (nor_25_out[4], and_27_out, nor_58_out);
  nor nor_58 (nor_58_out, nor_25_out[4], and_58_out);
  nor nor_59 (nor_25_out[5], and_27_out, nor_60_out);
  nor nor_60 (nor_60_out, nor_25_out[5], and_73_out);
  nor nor_61 (nor_25_out[6], and_27_out, nor_62_out);
  nor nor_62 (nor_62_out, nor_25_out[6], and_74_out);
  nor nor_63 (nor_25_out[7], and_27_out, nor_64_out);
  nor nor_64 (nor_64_out, nor_25_out[7], and_83_out);
  and and_84 (_12[7], and_1_out[12], nor_25_out[7], Read);
  and and_85 (and_85_out, and_1_out[1], Reset);
  and and_86 (and_86_out, and_1_out[5], Reset);
  and and_87 (and_87_out, and_1_out[9], Reset);
  and and_88 (and_88_out, and_1_out[13], Reset);
  and and_89 (and_89_out, and_1_out[1], Data_In[0], Set);
  and and_90 (and_90_out, and_1_out[1], Data_In[1], Set);
  and and_91 (_1[0], and_1_out[1], nor_65_out[0], Read);
  and and_92 (_1[1], and_1_out[1], nor_65_out[1], Read);
  and and_93 (and_93_out, and_1_out[5], Data_In[1], Set);
  and and_94 (and_94_out, and_1_out[5], Data_In[0], Set);
  and and_95 (_5[0], and_1_out[5], nor_73_out[0], Read);
  and and_96 (_5[1], and_1_out[5], nor_73_out[1], Read);
  and and_97 (and_97_out, and_1_out[9], Data_In[1], Set);
  and and_98 (and_98_out, and_1_out[9], Data_In[0], Set);
  and and_99 (_9[0], and_1_out[9], nor_81_out[0], Read);
  and and_100 (_9[1], and_1_out[9], nor_81_out[1], Read);
  and and_101 (and_101_out, and_1_out[13], Data_In[1], Set);
  and and_102 (and_102_out, and_1_out[13], Data_In[0], Set);
  and and_103 (_13[0], and_1_out[13], nor_89_out[0], Read);
  and and_104 (_13[1], and_1_out[13], nor_89_out[1], Read);
  and and_105 (and_105_out, and_1_out[1], Data_In[3], Set);
  and and_106 (and_106_out, and_1_out[1], Data_In[2], Set);
  nor nor_65 (nor_65_out[0], and_85_out, nor_66_out);
  nor nor_66 (nor_66_out, nor_65_out[0], and_89_out);
  nor nor_67 (nor_65_out[1], and_85_out, nor_68_out);
  nor nor_68 (nor_68_out, nor_65_out[1], and_90_out);
  nor nor_69 (nor_65_out[2], and_85_out, nor_70_out);
  nor nor_70 (nor_70_out, nor_65_out[2], and_106_out);
  nor nor_71 (nor_65_out[3], and_85_out, nor_72_out);
  nor nor_72 (nor_72_out, nor_65_out[3], and_105_out);
  and and_107 (_1[3], and_1_out[1], nor_65_out[3], Read);
  and and_108 (_1[2], and_1_out[1], nor_65_out[2], Read);
  and and_109 (and_109_out, and_1_out[5], Data_In[3], Set);
  and and_110 (and_110_out, and_1_out[5], Data_In[2], Set);
  nor nor_73 (nor_73_out[0], and_86_out, nor_74_out);
  nor nor_74 (nor_74_out, nor_73_out[0], and_94_out);
  nor nor_75 (nor_73_out[1], and_86_out, nor_76_out);
  nor nor_76 (nor_76_out, nor_73_out[1], and_93_out);
  nor nor_77 (nor_73_out[2], and_86_out, nor_78_out);
  nor nor_78 (nor_78_out, nor_73_out[2], and_110_out);
  nor nor_79 (nor_73_out[3], and_86_out, nor_80_out);
  nor nor_80 (nor_80_out, nor_73_out[3], and_109_out);
  and and_111 (_5[3], and_1_out[5], nor_73_out[3], Read);
  and and_112 (_5[2], and_1_out[5], nor_73_out[2], Read);
  and and_113 (and_113_out, and_1_out[9], Data_In[3], Set);
  and and_114 (and_114_out, and_1_out[9], Data_In[2], Set);
  nor nor_81 (nor_81_out[0], and_87_out, nor_82_out);
  nor nor_82 (nor_82_out, nor_81_out[0], and_98_out);
  nor nor_83 (nor_81_out[1], and_87_out, nor_84_out);
  nor nor_84 (nor_84_out, nor_81_out[1], and_97_out);
  nor nor_85 (nor_81_out[2], and_87_out, nor_86_out);
  nor nor_86 (nor_86_out, nor_81_out[2], and_114_out);
  nor nor_87 (nor_81_out[3], and_87_out, nor_88_out);
  nor nor_88 (nor_88_out, nor_81_out[3], and_113_out);
  and and_115 (_9[2], and_1_out[9], nor_81_out[2], Read);
  and and_116 (_9[3], and_1_out[9], nor_81_out[3], Read);
  and and_117 (and_117_out, and_1_out[13], Data_In[2], Set);
  and and_118 (and_118_out, and_1_out[13], Data_In[3], Set);
  nor nor_89 (nor_89_out[0], and_88_out, nor_90_out);
  nor nor_90 (nor_90_out, nor_89_out[0], and_102_out);
  nor nor_91 (nor_89_out[1], and_88_out, nor_92_out);
  nor nor_92 (nor_92_out, nor_89_out[1], and_101_out);
  nor nor_93 (nor_89_out[2], and_88_out, nor_94_out);
  nor nor_94 (nor_94_out, nor_89_out[2], and_117_out);
  nor nor_95 (nor_89_out[3], and_88_out, nor_96_out);
  nor nor_96 (nor_96_out, nor_89_out[3], and_118_out);
  and and_119 (_13[2], and_1_out[13], nor_89_out[2], Read);
  and and_120 (_13[3], and_1_out[13], nor_89_out[3], Read);
  and and_121 (and_121_out, and_1_out[1], Data_In[4], Set);
  and and_122 (and_122_out, and_1_out[1], Data_In[5], Set);
  and and_123 (_1[4], and_1_out[1], nor_65_out[4], Read);
  and and_124 (_1[5], and_1_out[1], nor_65_out[5], Read);
  and and_125 (and_125_out, and_1_out[5], Data_In[4], Set);
  and and_126 (and_126_out, and_1_out[5], Data_In[5], Set);
  and and_127 (_5[4], and_1_out[5], nor_73_out[4], Read);
  and and_128 (_5[5], and_1_out[5], nor_73_out[5], Read);
  and and_129 (and_129_out, and_1_out[9], Data_In[5], Set);
  and and_130 (and_130_out, and_1_out[9], Data_In[4], Set);
  and and_131 (_9[4], and_1_out[9], nor_81_out[4], Read);
  and and_132 (_9[5], and_1_out[9], nor_81_out[5], Read);
  and and_133 (and_133_out, and_1_out[13], Data_In[4], Set);
  and and_134 (and_134_out, and_1_out[13], Data_In[5], Set);
  and and_135 (_13[4], and_1_out[13], nor_89_out[4], Read);
  and and_136 (_13[5], and_1_out[13], nor_89_out[5], Read);
  and and_137 (and_137_out, and_1_out[1], Data_In[6], Set);
  and and_138 (and_138_out, and_1_out[1], Data_In[7], Set);
  nor nor_97 (nor_65_out[4], and_85_out, nor_98_out);
  nor nor_98 (nor_98_out, nor_65_out[4], and_121_out);
  nor nor_99 (nor_65_out[5], and_85_out, nor_100_out);
  nor nor_100 (nor_100_out, nor_65_out[5], and_122_out);
  nor nor_101 (nor_65_out[6], and_85_out, nor_102_out);
  nor nor_102 (nor_102_out, nor_65_out[6], and_137_out);
  nor nor_103 (nor_65_out[7], and_85_out, nor_104_out);
  nor nor_104 (nor_104_out, nor_65_out[7], and_138_out);
  and and_139 (_1[7], and_1_out[1], nor_65_out[7], Read);
  and and_140 (_1[6], and_1_out[1], nor_65_out[6], Read);
  and and_141 (and_141_out, and_1_out[5], Data_In[6], Set);
  and and_142 (and_142_out, and_1_out[5], Data_In[7], Set);
  nor nor_105 (nor_73_out[4], and_86_out, nor_106_out);
  nor nor_106 (nor_106_out, nor_73_out[4], and_125_out);
  nor nor_107 (nor_73_out[5], and_86_out, nor_108_out);
  nor nor_108 (nor_108_out, nor_73_out[5], and_126_out);
  nor nor_109 (nor_73_out[6], and_86_out, nor_110_out);
  nor nor_110 (nor_110_out, nor_73_out[6], and_141_out);
  nor nor_111 (nor_73_out[7], and_86_out, nor_112_out);
  nor nor_112 (nor_112_out, nor_73_out[7], and_142_out);
  and and_143 (_5[7], and_1_out[5], nor_73_out[7], Read);
  and and_144 (_5[6], and_1_out[5], nor_73_out[6], Read);
  and and_145 (and_145_out, and_1_out[9], Data_In[6], Set);
  and and_146 (and_146_out, and_1_out[9], Data_In[7], Set);
  nor nor_113 (nor_81_out[4], and_87_out, nor_114_out);
  nor nor_114 (nor_114_out, nor_81_out[4], and_130_out);
  nor nor_115 (nor_81_out[5], and_87_out, nor_116_out);
  nor nor_116 (nor_116_out, nor_81_out[5], and_129_out);
  nor nor_117 (nor_81_out[6], and_87_out, nor_118_out);
  nor nor_118 (nor_118_out, nor_81_out[6], and_145_out);
  nor nor_119 (nor_81_out[7], and_87_out, nor_120_out);
  nor nor_120 (nor_120_out, nor_81_out[7], and_146_out);
  and and_147 (_9[7], and_1_out[9], nor_81_out[7], Read);
  and and_148 (_9[6], and_1_out[9], nor_81_out[6], Read);
  and and_149 (and_149_out, and_1_out[13], Data_In[7], Set);
  and and_150 (and_150_out, and_1_out[13], Data_In[6], Set);
  nor nor_121 (nor_89_out[4], and_88_out, nor_122_out);
  nor nor_122 (nor_122_out, nor_89_out[4], and_133_out);
  nor nor_123 (nor_89_out[5], and_88_out, nor_124_out);
  nor nor_124 (nor_124_out, nor_89_out[5], and_134_out);
  nor nor_125 (nor_89_out[6], and_88_out, nor_126_out);
  nor nor_126 (nor_126_out, nor_89_out[6], and_150_out);
  nor nor_127 (nor_89_out[7], and_88_out, nor_128_out);
  nor nor_128 (nor_128_out, nor_89_out[7], and_149_out);
  and and_151 (_13[6], and_1_out[13], nor_89_out[6], Read);
  and and_152 (_13[7], and_1_out[13], nor_89_out[7], Read);
  and and_153 (and_153_out, and_1_out[2], Reset);
  and and_154 (and_154_out, and_1_out[6], Reset);
  and and_155 (and_155_out, and_1_out[10], Reset);
  and and_156 (and_156_out, and_1_out[14], Reset);
  and and_157 (and_157_out, and_1_out[2], Data_In[1], Set);
  and and_158 (and_158_out, and_1_out[2], Data_In[0], Set);
  and and_159 (_2[0], and_1_out[2], nor_129_out[0], Read);
  and and_160 (_2[1], and_1_out[2], nor_129_out[1], Read);
  and and_161 (and_161_out, and_1_out[6], Data_In[1], Set);
  and and_162 (and_162_out, and_1_out[6], Data_In[0], Set);
  and and_163 (_6[1], and_1_out[6], nor_137_out[1], Read);
  and and_164 (_6[0], and_1_out[6], nor_137_out[0], Read);
  and and_165 (and_165_out, and_1_out[10], Data_In[1], Set);
  and and_166 (and_166_out, and_1_out[10], Data_In[0], Set);
  and and_167 (_10[0], and_1_out[10], nor_145_out[0], Read);
  and and_168 (_10[1], and_1_out[10], nor_145_out[1], Read);
  and and_169 (and_169_out, and_1_out[14], Data_In[0], Set);
  and and_170 (and_170_out, and_1_out[14], Data_In[1], Set);
  and and_171 (_14[0], and_1_out[14], nor_153_out[0], Read);
  and and_172 (_14[1], and_1_out[14], nor_153_out[1], Read);
  and and_173 (and_173_out, and_1_out[2], Data_In[3], Set);
  and and_174 (and_174_out, and_1_out[2], Data_In[2], Set);
  nor nor_129 (nor_129_out[0], and_153_out, nor_130_out);
  nor nor_130 (nor_130_out, nor_129_out[0], and_158_out);
  nor nor_131 (nor_129_out[1], and_153_out, nor_132_out);
  nor nor_132 (nor_132_out, nor_129_out[1], and_157_out);
  nor nor_133 (nor_129_out[2], and_153_out, nor_134_out);
  nor nor_134 (nor_134_out, nor_129_out[2], and_174_out);
  nor nor_135 (nor_129_out[3], and_153_out, nor_136_out);
  nor nor_136 (nor_136_out, nor_129_out[3], and_173_out);
  and and_175 (_2[2], and_1_out[2], nor_129_out[2], Read);
  and and_176 (_2[3], and_1_out[2], nor_129_out[3], Read);
  and and_177 (and_177_out, and_1_out[6], Data_In[2], Set);
  and and_178 (and_178_out, and_1_out[6], Data_In[3], Set);
  nor nor_137 (nor_137_out[0], and_154_out, nor_138_out);
  nor nor_138 (nor_138_out, nor_137_out[0], and_162_out);
  nor nor_139 (nor_137_out[1], and_154_out, nor_140_out);
  nor nor_140 (nor_140_out, nor_137_out[1], and_161_out);
  nor nor_141 (nor_137_out[2], and_154_out, nor_142_out);
  nor nor_142 (nor_142_out, nor_137_out[2], and_177_out);
  nor nor_143 (nor_137_out[3], and_154_out, nor_144_out);
  nor nor_144 (nor_144_out, nor_137_out[3], and_178_out);
  and and_179 (_6[3], and_1_out[6], nor_137_out[3], Read);
  and and_180 (_6[2], and_1_out[6], nor_137_out[2], Read);
  and and_181 (and_181_out, and_1_out[10], Data_In[2], Set);
  and and_182 (and_182_out, and_1_out[10], Data_In[3], Set);
  nor nor_145 (nor_145_out[0], and_155_out, nor_146_out);
  nor nor_146 (nor_146_out, nor_145_out[0], and_166_out);
  nor nor_147 (nor_145_out[1], and_155_out, nor_148_out);
  nor nor_148 (nor_148_out, nor_145_out[1], and_165_out);
  nor nor_149 (nor_145_out[2], and_155_out, nor_150_out);
  nor nor_150 (nor_150_out, nor_145_out[2], and_181_out);
  nor nor_151 (nor_145_out[3], and_155_out, nor_152_out);
  nor nor_152 (nor_152_out, nor_145_out[3], and_182_out);
  and and_183 (_10[3], and_1_out[10], nor_145_out[3], Read);
  and and_184 (_10[2], and_1_out[10], nor_145_out[2], Read);
  and and_185 (and_185_out, and_1_out[14], Data_In[3], Set);
  and and_186 (and_186_out, and_1_out[14], Data_In[2], Set);
  nor nor_153 (nor_153_out[0], and_156_out, nor_154_out);
  nor nor_154 (nor_154_out, nor_153_out[0], and_169_out);
  nor nor_155 (nor_153_out[1], and_156_out, nor_156_out);
  nor nor_156 (nor_156_out, nor_153_out[1], and_170_out);
  nor nor_157 (nor_153_out[2], and_156_out, nor_158_out);
  nor nor_158 (nor_158_out, nor_153_out[2], and_186_out);
  nor nor_159 (nor_153_out[3], and_156_out, nor_160_out);
  nor nor_160 (nor_160_out, nor_153_out[3], and_185_out);
  and and_187 (_14[3], and_1_out[14], nor_153_out[3], Read);
  and and_188 (_14[2], and_1_out[14], nor_153_out[2], Read);
  and and_189 (and_189_out, and_1_out[2], Data_In[4], Set);
  and and_190 (and_190_out, and_1_out[2], Data_In[5], Set);
  and and_191 (_2[5], and_1_out[2], nor_129_out[5], Read);
  and and_192 (_2[4], and_1_out[2], nor_129_out[4], Read);
  and and_193 (and_193_out, and_1_out[6], Data_In[4], Set);
  and and_194 (and_194_out, and_1_out[6], Data_In[5], Set);
  and and_195 (_6[4], and_1_out[6], nor_137_out[4], Read);
  and and_196 (_6[5], and_1_out[6], nor_137_out[5], Read);
  and and_197 (and_197_out, and_1_out[10], Data_In[4], Set);
  and and_198 (and_198_out, and_1_out[10], Data_In[5], Set);
  and and_199 (_10[4], and_1_out[10], nor_145_out[4], Read);
  and and_200 (_10[5], and_1_out[10], nor_145_out[5], Read);
  and and_201 (and_201_out, and_1_out[14], Data_In[5], Set);
  and and_202 (and_202_out, and_1_out[14], Data_In[4], Set);
  and and_203 (_14[4], and_1_out[14], nor_153_out[4], Read);
  and and_204 (_14[5], and_1_out[14], nor_153_out[5], Read);
  and and_205 (and_205_out, and_1_out[2], Data_In[6], Set);
  and and_206 (and_206_out, and_1_out[2], Data_In[7], Set);
  nor nor_161 (nor_129_out[4], and_153_out, nor_162_out);
  nor nor_162 (nor_162_out, nor_129_out[4], and_189_out);
  nor nor_163 (nor_129_out[5], and_153_out, nor_164_out);
  nor nor_164 (nor_164_out, nor_129_out[5], and_190_out);
  nor nor_165 (nor_129_out[6], and_153_out, nor_166_out);
  nor nor_166 (nor_166_out, nor_129_out[6], and_205_out);
  nor nor_167 (nor_129_out[7], and_153_out, nor_168_out);
  nor nor_168 (nor_168_out, nor_129_out[7], and_206_out);
  and and_207 (_2[6], and_1_out[2], nor_129_out[6], Read);
  and and_208 (_2[7], and_1_out[2], nor_129_out[7], Read);
  and and_209 (and_209_out, and_1_out[6], Data_In[7], Set);
  and and_210 (and_210_out, and_1_out[6], Data_In[6], Set);
  nor nor_169 (nor_137_out[4], and_154_out, nor_170_out);
  nor nor_170 (nor_170_out, nor_137_out[4], and_193_out);
  nor nor_171 (nor_137_out[5], and_154_out, nor_172_out);
  nor nor_172 (nor_172_out, nor_137_out[5], and_194_out);
  nor nor_173 (nor_137_out[6], and_154_out, nor_174_out);
  nor nor_174 (nor_174_out, nor_137_out[6], and_210_out);
  nor nor_175 (nor_137_out[7], and_154_out, nor_176_out);
  nor nor_176 (nor_176_out, nor_137_out[7], and_209_out);
  and and_211 (_6[6], and_1_out[6], nor_137_out[6], Read);
  and and_212 (_6[7], and_1_out[6], nor_137_out[7], Read);
  and and_213 (and_213_out, and_1_out[10], Data_In[7], Set);
  and and_214 (and_214_out, and_1_out[10], Data_In[6], Set);
  nor nor_177 (nor_145_out[4], and_155_out, nor_178_out);
  nor nor_178 (nor_178_out, nor_145_out[4], and_197_out);
  nor nor_179 (nor_145_out[5], and_155_out, nor_180_out);
  nor nor_180 (nor_180_out, nor_145_out[5], and_198_out);
  nor nor_181 (nor_145_out[6], and_155_out, nor_182_out);
  nor nor_182 (nor_182_out, nor_145_out[6], and_214_out);
  nor nor_183 (nor_145_out[7], and_155_out, nor_184_out);
  nor nor_184 (nor_184_out, nor_145_out[7], and_213_out);
  and and_215 (_10[7], and_1_out[10], nor_145_out[7], Read);
  and and_216 (_10[6], and_1_out[10], nor_145_out[6], Read);
  and and_217 (and_217_out, and_1_out[14], Data_In[6], Set);
  and and_218 (and_218_out, and_1_out[14], Data_In[7], Set);
  nor nor_185 (nor_153_out[4], and_156_out, nor_186_out);
  nor nor_186 (nor_186_out, nor_153_out[4], and_202_out);
  nor nor_187 (nor_153_out[5], and_156_out, nor_188_out);
  nor nor_188 (nor_188_out, nor_153_out[5], and_201_out);
  nor nor_189 (nor_153_out[6], and_156_out, nor_190_out);
  nor nor_190 (nor_190_out, nor_153_out[6], and_217_out);
  nor nor_191 (nor_153_out[7], and_156_out, nor_192_out);
  nor nor_192 (nor_192_out, nor_153_out[7], and_218_out);
  and and_219 (_14[7], and_1_out[14], nor_153_out[7], Read);
  and and_220 (_14[6], and_1_out[14], nor_153_out[6], Read);
  and and_221 (and_221_out, and_1_out[3], Reset);
  and and_222 (and_222_out, and_1_out[3], Data_In[0], Set);
  and and_223 (_3[0], and_1_out[3], nor_193_out[0], Read);
  and and_224 (and_224_out, and_1_out[7], Data_In[0], Set);
  and and_225 (and_225_out, and_1_out[7], Reset);
  and and_226 (_7[0], and_1_out[7], nor_201_out[0], Read);
  and and_227 (and_227_out, and_1_out[11], Reset);
  and and_228 (and_228_out, and_1_out[11], Data_In[0], Set);
  and and_229 (_11[0], and_1_out[11], nor_209_out[0], Read);
  and and_230 (and_230_out, and_1_out[15], Data_In[0], Set);
  and and_231 (and_231_out, and_1_out[15], Reset);
  and and_232 (_15[0], and_1_out[15], nor_217_out[0], Read);
  and and_233 (and_233_out, and_1_out[3], Data_In[2], Set);
  and and_234 (and_234_out, and_1_out[3], Data_In[1], Set);
  nor nor_193 (nor_193_out[0], and_221_out, nor_194_out);
  nor nor_194 (nor_194_out, nor_193_out[0], and_222_out);
  nor nor_195 (nor_193_out[1], and_221_out, nor_196_out);
  nor nor_196 (nor_196_out, nor_193_out[1], and_234_out);
  nor nor_197 (nor_193_out[2], and_221_out, nor_198_out);
  nor nor_198 (nor_198_out, nor_193_out[2], and_233_out);
  nor nor_199 (nor_193_out[3], and_221_out, nor_200_out);
  nor nor_200 (nor_200_out, nor_193_out[3], and_249_out);
  and and_235 (_3[2], and_1_out[3], nor_193_out[2], Read);
  and and_236 (_3[1], and_1_out[3], nor_193_out[1], Read);
  and and_237 (and_237_out, and_1_out[7], Data_In[1], Set);
  and and_238 (and_238_out, and_1_out[7], Data_In[2], Set);
  nor nor_201 (nor_201_out[0], and_225_out, nor_202_out);
  nor nor_202 (nor_202_out, nor_201_out[0], and_224_out);
  nor nor_203 (nor_201_out[1], and_225_out, nor_204_out);
  nor nor_204 (nor_204_out, nor_201_out[1], and_237_out);
  nor nor_205 (nor_201_out[2], and_225_out, nor_206_out);
  nor nor_206 (nor_206_out, nor_201_out[2], and_238_out);
  nor nor_207 (nor_201_out[3], and_225_out, nor_208_out);
  nor nor_208 (nor_208_out, nor_201_out[3], and_253_out);
  and and_239 (_7[1], and_1_out[7], nor_201_out[1], Read);
  and and_240 (_7[2], and_1_out[7], nor_201_out[2], Read);
  and and_241 (and_241_out, and_1_out[11], Data_In[1], Set);
  and and_242 (and_242_out, and_1_out[11], Data_In[2], Set);
  nor nor_209 (nor_209_out[0], and_227_out, nor_210_out);
  nor nor_210 (nor_210_out, nor_209_out[0], and_228_out);
  nor nor_211 (nor_209_out[1], and_227_out, nor_212_out);
  nor nor_212 (nor_212_out, nor_209_out[1], and_241_out);
  nor nor_213 (nor_209_out[2], and_227_out, nor_214_out);
  nor nor_214 (nor_214_out, nor_209_out[2], and_242_out);
  nor nor_215 (nor_209_out[3], and_227_out, nor_216_out);
  nor nor_216 (nor_216_out, nor_209_out[3], and_257_out);
  and and_243 (_11[1], and_1_out[11], nor_209_out[1], Read);
  and and_244 (_11[2], and_1_out[11], nor_209_out[2], Read);
  and and_245 (and_245_out, and_1_out[15], Data_In[2], Set);
  and and_246 (and_246_out, and_1_out[15], Data_In[1], Set);
  nor nor_217 (nor_217_out[0], and_231_out, nor_218_out);
  nor nor_218 (nor_218_out, nor_217_out[0], and_230_out);
  nor nor_219 (nor_217_out[1], and_231_out, nor_220_out);
  nor nor_220 (nor_220_out, nor_217_out[1], and_246_out);
  nor nor_221 (nor_217_out[2], and_231_out, nor_222_out);
  nor nor_222 (nor_222_out, nor_217_out[2], and_245_out);
  nor nor_223 (nor_217_out[3], and_231_out, nor_224_out);
  nor nor_224 (nor_224_out, nor_217_out[3], and_261_out);
  and and_247 (_15[1], and_1_out[15], nor_217_out[1], Read);
  and and_248 (_15[2], and_1_out[15], nor_217_out[2], Read);
  and and_249 (and_249_out, and_1_out[3], Data_In[3], Set);
  and and_250 (and_250_out, and_1_out[3], Data_In[4], Set);
  and and_251 (_3[4], and_1_out[3], nor_193_out[4], Read);
  and and_252 (_3[3], and_1_out[3], nor_193_out[3], Read);
  and and_253 (and_253_out, and_1_out[7], Data_In[3], Set);
  and and_254 (and_254_out, and_1_out[7], Data_In[4], Set);
  and and_255 (_7[3], and_1_out[7], nor_201_out[3], Read);
  and and_256 (_7[4], and_1_out[7], nor_201_out[4], Read);
  and and_257 (and_257_out, and_1_out[11], Data_In[3], Set);
  and and_258 (and_258_out, and_1_out[11], Data_In[4], Set);
  and and_259 (_11[3], and_1_out[11], nor_209_out[3], Read);
  and and_260 (_11[4], and_1_out[11], nor_209_out[4], Read);
  and and_261 (and_261_out, and_1_out[15], Data_In[3], Set);
  and and_262 (and_262_out, and_1_out[15], Data_In[4], Set);
  and and_263 (_15[4], and_1_out[15], nor_217_out[4], Read);
  and and_264 (_15[3], and_1_out[15], nor_217_out[3], Read);
  and and_265 (and_265_out, and_1_out[3], Data_In[5], Set);
  and and_266 (and_266_out, and_1_out[3], Data_In[6], Set);
  nor nor_225 (nor_193_out[4], and_221_out, nor_226_out);
  nor nor_226 (nor_226_out, nor_193_out[4], and_250_out);
  nor nor_227 (nor_193_out[5], and_221_out, nor_228_out);
  nor nor_228 (nor_228_out, nor_193_out[5], and_265_out);
  nor nor_229 (nor_193_out[6], and_221_out, nor_230_out);
  nor nor_230 (nor_230_out, nor_193_out[6], and_266_out);
  nor nor_231 (nor_193_out[7], and_221_out, nor_232_out);
  nor nor_232 (nor_232_out, nor_193_out[7], and_281_out);
  and and_267 (_3[5], and_1_out[3], nor_193_out[5], Read);
  and and_268 (_3[6], and_1_out[3], nor_193_out[6], Read);
  and and_269 (and_269_out, and_1_out[7], Data_In[5], Set);
  and and_270 (and_270_out, and_1_out[7], Data_In[6], Set);
  nor nor_233 (nor_201_out[4], and_225_out, nor_234_out);
  nor nor_234 (nor_234_out, nor_201_out[4], and_254_out);
  nor nor_235 (nor_201_out[5], and_225_out, nor_236_out);
  nor nor_236 (nor_236_out, nor_201_out[5], and_269_out);
  nor nor_237 (nor_201_out[6], and_225_out, nor_238_out);
  nor nor_238 (nor_238_out, nor_201_out[6], and_270_out);
  nor nor_239 (nor_201_out[7], and_225_out, nor_240_out);
  nor nor_240 (nor_240_out, nor_201_out[7], and_283_out);
  and and_271 (_7[5], and_1_out[7], nor_201_out[5], Read);
  and and_272 (_7[6], and_1_out[7], nor_201_out[6], Read);
  and and_273 (and_273_out, and_1_out[11], Data_In[6], Set);
  and and_274 (and_274_out, and_1_out[11], Data_In[5], Set);
  nor nor_241 (nor_209_out[4], and_227_out, nor_242_out);
  nor nor_242 (nor_242_out, nor_209_out[4], and_258_out);
  nor nor_243 (nor_209_out[5], and_227_out, nor_244_out);
  nor nor_244 (nor_244_out, nor_209_out[5], and_274_out);
  nor nor_245 (nor_209_out[6], and_227_out, nor_246_out);
  nor nor_246 (nor_246_out, nor_209_out[6], and_273_out);
  nor nor_247 (nor_209_out[7], and_227_out, nor_248_out);
  nor nor_248 (nor_248_out, nor_209_out[7], and_285_out);
  and and_275 (_11[6], and_1_out[11], nor_209_out[6], Read);
  and and_276 (_11[5], and_1_out[11], nor_209_out[5], Read);
  and and_277 (and_277_out, and_1_out[15], Data_In[5], Set);
  and and_278 (and_278_out, and_1_out[15], Data_In[6], Set);
  nor nor_249 (nor_217_out[4], and_231_out, nor_250_out);
  nor nor_250 (nor_250_out, nor_217_out[4], and_262_out);
  nor nor_251 (nor_217_out[5], and_231_out, nor_252_out);
  nor nor_252 (nor_252_out, nor_217_out[5], and_277_out);
  nor nor_253 (nor_217_out[6], and_231_out, nor_254_out);
  nor nor_254 (nor_254_out, nor_217_out[6], and_278_out);
  nor nor_255 (nor_217_out[7], and_231_out, nor_256_out);
  nor nor_256 (nor_256_out, nor_217_out[7], and_287_out);
  and and_279 (_15[5], and_1_out[15], nor_217_out[5], Read);
  and and_280 (_15[6], and_1_out[15], nor_217_out[6], Read);
  and and_281 (and_281_out, and_1_out[3], Data_In[7], Set);
  and and_282 (_3[7], and_1_out[3], nor_193_out[7], Read);
  and and_283 (and_283_out, and_1_out[7], Data_In[7], Set);
  and and_284 (_7[7], and_1_out[7], nor_201_out[7], Read);
  and and_285 (and_285_out, and_1_out[11], Data_In[7], Set);
  and and_286 (_11[7], and_1_out[11], nor_209_out[7], Read);
  and and_287 (and_287_out, and_1_out[15], Data_In[7], Set);
  and and_288 (_15[7], and_1_out[15], nor_217_out[7], Read);
endmodule

module ALU (
  input  RSH,
  input  OR,
  input  FC,
  input  CIn,
  input  [7:0] Reg_A,
  input  [7:0] Reg_B,
  input  nA,
  input  nB,
  output [7:0] Reg_C
);

  wire and_1_out, and_2_out, and_3_out, and_4_out, and_5_out, and_6_out, and_7_out, and_8_out, and_9_out,
       and_10_out, and_11_out, and_12_out, and_13_out, and_14_out, and_15_out, and_16_out, and_17_out,
       and_18_out, and_19_out, and_20_out, and_21_out, and_22_out, and_23_out, and_24_out, and_25_out,
       and_26_out, and_27_out, and_28_out, and_29_out, and_30_out, and_31_out, and_32_out, and_33_out,
       and_34_out, and_35_out, and_36_out, and_37_out, and_38_out, and_39_out, and_40_out, and_41_out,
       and_42_out, and_43_out, and_44_out, and_45_out, and_46_out, and_47_out, and_48_out, and_49_out,
       and_50_out, and_51_out, and_52_out, and_53_out, and_54_out, nor_1_out, nor_2_out, nor_3_out,
       nor_4_out, nor_5_out, nor_6_out, nor_7_out, nor_8_out, nor_9_out, nor_10_out, nor_11_out, nor_12_out,
       nor_13_out, nor_14_out, nor_15_out, nor_16_out, or_1_out, or_2_out, or_3_out, or_4_out, or_5_out,
       or_6_out, or_7_out, or_8_out, or_9_out, or_10_out, or_11_out, or_12_out, or_13_out, or_14_out,
       or_15_out, or_16_out, or_17_out, or_18_out, or_19_out, or_20_out, or_21_out, or_22_out, or_23_out,
       or_24_out, or_25_out, xnor_1_out, xnor_2_out, xnor_3_out, xnor_4_out, xnor_5_out, xnor_6_out,
       xnor_7_out, xnor_8_out, xnor_9_out, xnor_10_out, xnor_11_out, xnor_12_out, xnor_13_out, xnor_14_out,
       xnor_15_out, xnor_16_out, xor_1_out, xor_2_out, xor_3_out, xor_4_out, xor_5_out, xor_6_out, xor_7_out,
       xor_8_out;

  xnor xnor_1 (xnor_1_out, Reg_A[0], ~nA);  // XNOR_Gate
  xnor xnor_2 (xnor_2_out, Reg_B[0], ~nB);  // XNOR_Gate
  xnor xnor_3 (xnor_3_out, Reg_A[1], ~nA);  // XNOR_Gate
  xnor xnor_4 (xnor_4_out, Reg_B[1], ~nB);  // XNOR_Gate
  xnor xnor_5 (xnor_5_out, Reg_A[2], ~nA);  // XNOR_Gate
  xnor xnor_6 (xnor_6_out, Reg_B[2], ~nB);  // XNOR_Gate
  xnor xnor_7 (xnor_7_out, Reg_A[3], ~nA);  // XNOR_Gate
  xnor xnor_8 (xnor_8_out, Reg_B[3], ~nB);  // XNOR_Gate
  xnor xnor_9 (xnor_9_out, Reg_A[4], ~nA);  // XNOR_Gate
  xnor xnor_10 (xnor_10_out, Reg_B[4], ~nB);  // XNOR_Gate
  xnor xnor_11 (xnor_11_out, Reg_A[5], ~nA);  // XNOR_Gate
  xnor xnor_12 (xnor_12_out, Reg_B[5], ~nB);  // XNOR_Gate
  xnor xnor_13 (xnor_13_out, Reg_A[6], ~nA);  // XNOR_Gate
  xnor xnor_14 (xnor_14_out, Reg_B[6], ~nB);  // XNOR_Gate
  xnor xnor_15 (xnor_15_out, Reg_A[7], ~nA);  // XNOR_Gate
  xnor xnor_16 (xnor_16_out, Reg_B[7], ~nB);  // XNOR_Gate
  and and_1 (and_1_out, xnor_1_out, xnor_2_out);
  nor nor_1 (nor_1_out, xnor_1_out, xnor_2_out);
  and and_2 (and_2_out, xnor_3_out, xnor_4_out);
  nor nor_2 (nor_2_out, xnor_3_out, xnor_4_out);
  and and_3 (and_3_out, xnor_5_out, xnor_6_out);
  nor nor_3 (nor_3_out, xnor_5_out, xnor_6_out);
  and and_4 (and_4_out, xnor_7_out, xnor_8_out);
  nor nor_4 (nor_4_out, xnor_7_out, xnor_8_out);
  and and_5 (and_5_out, xnor_9_out, xnor_10_out);
  nor nor_5 (nor_5_out, xnor_9_out, xnor_10_out);
  and and_6 (and_6_out, xnor_11_out, xnor_12_out);
  nor nor_6 (nor_6_out, xnor_11_out, xnor_12_out);
  and and_7 (and_7_out, xnor_13_out, xnor_14_out);
  nor nor_7 (nor_7_out, xnor_13_out, xnor_14_out);
  and and_8 (and_8_out, xnor_15_out, xnor_16_out);
  nor nor_8 (nor_8_out, xnor_15_out, xnor_16_out);
  or or_1 (or_1_out, CIn, FC);
  nor nor_9 (nor_9_out, xnor_1_out, xnor_2_out);
  or or_2 (or_2_out, nor_9_out, and_1_out);
  and and_9 (and_9_out, and_1_out, or_2_out);
  and and_10 (and_10_out, or_1_out, ~or_2_out);  // AND_Gate
  or or_3 (or_3_out, and_9_out, and_10_out, FC);
  nor nor_10 (nor_10_out, xnor_3_out, xnor_4_out);
  or or_4 (or_4_out, nor_10_out, and_2_out);
  and and_11 (and_11_out, and_2_out, or_4_out);
  and and_12 (and_12_out, or_3_out, ~or_4_out);  // AND_Gate
  or or_5 (or_5_out, and_11_out, and_12_out, FC);
  nor nor_11 (nor_11_out, xnor_5_out, xnor_6_out);
  or or_6 (or_6_out, nor_11_out, and_3_out);
  and and_13 (and_13_out, and_3_out, or_6_out);
  and and_14 (and_14_out, or_5_out, ~or_6_out);  // AND_Gate
  or or_7 (or_7_out, and_13_out, and_14_out, FC);
  nor nor_12 (nor_12_out, xnor_7_out, xnor_8_out);
  or or_8 (or_8_out, nor_12_out, and_4_out);
  and and_15 (and_15_out, or_7_out, ~or_8_out);  // AND_Gate
  and and_16 (and_16_out, and_4_out, or_8_out);
  or or_9 (or_9_out, and_16_out, and_15_out, FC);
  nor nor_13 (nor_13_out, xnor_9_out, xnor_10_out);
  or or_10 (or_10_out, nor_13_out, and_5_out);
  and and_17 (and_17_out, and_5_out, or_10_out);
  and and_18 (and_18_out, or_9_out, ~or_10_out);  // AND_Gate
  or or_11 (or_11_out, and_17_out, and_18_out, FC);
  nor nor_14 (nor_14_out, xnor_11_out, xnor_12_out);
  or or_12 (or_12_out, nor_14_out, and_6_out);
  and and_19 (and_19_out, or_11_out, ~or_12_out);  // AND_Gate
  and and_20 (and_20_out, and_6_out, or_12_out);
  or or_13 (or_13_out, and_20_out, and_19_out, FC);
  nor nor_15 (nor_15_out, xnor_13_out, xnor_14_out);
  or or_14 (or_14_out, nor_15_out, and_7_out);
  and and_21 (and_21_out, or_13_out, ~or_14_out);  // AND_Gate
  and and_22 (and_22_out, and_7_out, or_14_out);
  or or_15 (or_15_out, and_22_out, and_21_out, FC);
  nor nor_16 (nor_16_out, xnor_15_out, xnor_16_out);
  or or_16 (or_16_out, nor_16_out, and_8_out);
  and and_23 (and_23_out, or_15_out, ~or_16_out);  // AND_Gate
  and and_24 (and_24_out, and_8_out, or_16_out);
  or or_17 (or_17_out, and_24_out, and_23_out);
  xor xor_1 (xor_1_out, ~or_2_out, or_1_out);  // XOR_Gate
  xor xor_2 (xor_2_out, ~or_4_out, or_3_out);  // XOR_Gate
  xor xor_3 (xor_3_out, ~or_6_out, or_5_out);  // XOR_Gate
  xor xor_4 (xor_4_out, ~or_8_out, or_7_out);  // XOR_Gate
  xor xor_5 (xor_5_out, ~or_10_out, or_9_out);  // XOR_Gate
  xor xor_6 (xor_6_out, ~or_12_out, or_11_out);  // XOR_Gate
  xor xor_7 (xor_7_out, ~or_14_out, or_13_out);  // XOR_Gate
  xor xor_8 (xor_8_out, ~or_16_out, or_15_out);  // XOR_Gate
  and and_25 (and_25_out, ~OR, xor_1_out);  // AND_Gate
  and and_26 (and_26_out, OR, nor_1_out);
  and and_27 (and_27_out, ~OR, xor_2_out);  // AND_Gate
  and and_28 (and_28_out, OR, nor_2_out);
  and and_29 (and_29_out, ~OR, xor_3_out);  // AND_Gate
  and and_30 (and_30_out, OR, nor_3_out);
  and and_31 (and_31_out, ~OR, xor_4_out);  // AND_Gate
  and and_32 (and_32_out, OR, nor_4_out);
  and and_33 (and_33_out, ~OR, xor_5_out);  // AND_Gate
  and and_34 (and_34_out, OR, nor_5_out);
  and and_35 (and_35_out, ~OR, xor_6_out);  // AND_Gate
  and and_36 (and_36_out, OR, nor_6_out);
  and and_37 (and_37_out, ~OR, xor_7_out);  // AND_Gate
  and and_38 (and_38_out, OR, nor_7_out);
  and and_39 (and_39_out, ~OR, xor_8_out);  // AND_Gate
  and and_40 (and_40_out, OR, nor_8_out);
  or or_18 (or_18_out, and_25_out, and_26_out);
  or or_19 (or_19_out, and_27_out, and_28_out);
  or or_20 (or_20_out, and_29_out, and_30_out);
  or or_21 (or_21_out, and_31_out, and_32_out);
  or or_22 (or_22_out, and_33_out, and_34_out);
  or or_23 (or_23_out, and_35_out, and_36_out);
  or or_24 (or_24_out, and_37_out, and_38_out);
  or or_25 (or_25_out, and_39_out, and_40_out);
  and and_41 (and_41_out, ~RSH, or_18_out);  // AND_Gate
  or or_26 (Reg_C[0], and_41_out, and_42_out);
  and and_42 (and_42_out, RSH, or_19_out);
  and and_43 (and_43_out, ~RSH, or_19_out);  // AND_Gate
  or or_27 (Reg_C[1], and_43_out, and_44_out);
  and and_44 (and_44_out, RSH, or_20_out);
  and and_45 (and_45_out, ~RSH, or_20_out);  // AND_Gate
  or or_28 (Reg_C[2], and_45_out, and_46_out);
  and and_46 (and_46_out, RSH, or_21_out);
  and and_47 (and_47_out, ~RSH, or_21_out);  // AND_Gate
  or or_29 (Reg_C[3], and_47_out, and_48_out);
  and and_48 (and_48_out, RSH, or_22_out);
  and and_49 (and_49_out, ~RSH, or_22_out);  // AND_Gate
  or or_30 (Reg_C[4], and_49_out, and_50_out);
  and and_50 (and_50_out, RSH, or_23_out);
  and and_51 (and_51_out, ~RSH, or_23_out);  // AND_Gate
  or or_31 (Reg_C[5], and_51_out, and_52_out);
  and and_52 (and_52_out, RSH, or_24_out);
  and and_53 (and_53_out, ~RSH, or_24_out);  // AND_Gate
  or or_32 (Reg_C[6], and_53_out, and_54_out);
  and and_54 (and_54_out, RSH, or_25_out);
  and and_55 (Reg_C[7], ~RSH, or_25_out);  // AND_Gate

  // Notes on the sheet:
  //   Cout = (A AND B) OR ((A XOR B) AND C)
  //   Cout = (A OR B) AND C
endmodule
